// Logisim project prototype.circ as structural Verilog: 2 circuits, main circuit main
module main (
);

  wire button_1_out, cdm_8_mark5_1_p1, cdm_8_mark5_1_p2, cdm_8_mark5_1_p4, cdm_8_mark5_1_p5,
       cdm_8_mark5_1_p7, cdm_8_mark5_1_p8, cdm_8_mark5_1_p9, cdm_8_mark5_1_p10, cdm_8_mark5_1_p11, clock,
       code, data, not_1_out, read, video;
  wire [6:0] vaddr;
  wire [7:0] cdm_8_mark5_1_p14, cdm_8_mark5_1_p15, controlled_buffer_1_out;
  wire [7:7] adder_1_out;
  wire [15:0] cdm_8_mark5_1_p13;
  wire [31:0] video_buffer_1_row0, video_buffer_1_row1, video_buffer_1_row2, video_buffer_1_row3,
       video_buffer_1_row4, video_buffer_1_row5, video_buffer_1_row6, video_buffer_1_row7,
       video_buffer_1_row8, video_buffer_1_row9, video_buffer_1_row10, video_buffer_1_row11,
       video_buffer_1_row12, video_buffer_1_row13, video_buffer_1_row14, video_buffer_1_row15,
       video_buffer_1_row16, video_buffer_1_row17, video_buffer_1_row18, video_buffer_1_row19,
       video_buffer_1_row20, video_buffer_1_row21, video_buffer_1_row22, video_buffer_1_row23,
       video_buffer_1_row24, video_buffer_1_row25, video_buffer_1_row26, video_buffer_1_row27,
       video_buffer_1_row28, video_buffer_1_row29, video_buffer_1_row30, video_buffer_1_row31;

  // Probe on cdm_8_mark5_1_p1
  // Probe on cdm_8_mark5_1_p4
  // Probe on cdm_8_mark5_1_p2
  // Probe on cdm_8_mark5_1_p5
  Button button_1 (.out(button_1_out));
  Clock clock_1 (.out(clock));
  // Probe on cdm_8_mark5_1_p8
  // Probe on cdm_8_mark5_1_p9
  // Probe on cdm_8_mark5_1_p7
  // CdM_8_mark5 cdm_8_mark5_1: pin names not known; wires that end beside it: cdm_8_mark5_1_p1, cdm_8_mark5_1_p2, clock, cdm_8_mark5_1_p4, cdm_8_mark5_1_p5, button_1_out, cdm_8_mark5_1_p7, cdm_8_mark5_1_p8, cdm_8_mark5_1_p9, cdm_8_mark5_1_p10, cdm_8_mark5_1_p11, read, cdm_8_mark5_1_p13, cdm_8_mark5_1_p14, cdm_8_mark5_1_p15
  Decoder #(.disabled(0)) decoder_1 (.out0(code), .out1(data), .sel(cdm_8_mark5_1_p10), .en(cdm_8_mark5_1_p11));
  assign controlled_buffer_1_out = not_1_out ? cdm_8_mark5_1_p14 : 8'bz;  // Controlled_Buffer controlled_buffer_1
  not not_1 (not_1_out, read);
  assign cdm_8_mark5_1_p15 = read ? controlled_buffer_1_out : 8'bz;  // Controlled_Buffer controlled_buffer_2
  // Probe on cdm_8_mark5_1_p13
  // Probe on controlled_buffer_1_out
  // Probe on cdm_8_mark5_1_p13[7:0]
  Adder adder_1 (.a(cdm_8_mark5_1_p13[7:0]), .b(8'h20), .out({adder_1_out[7], vaddr}));  // open: cin, cout
  video_buffer video_buffer_1 (
    .vaddr({1'b0, vaddr}), .read(read), .video(video), .clock(clock), .data(controlled_buffer_1_out),
    .row0(video_buffer_1_row0), .row16(video_buffer_1_row16), .row1(video_buffer_1_row1),
    .row17(video_buffer_1_row17), .row2(video_buffer_1_row2), .row18(video_buffer_1_row18),
    .row3(video_buffer_1_row3), .row19(video_buffer_1_row19), .row4(video_buffer_1_row4),
    .row20(video_buffer_1_row20), .row5(video_buffer_1_row5), .row21(video_buffer_1_row21),
    .row6(video_buffer_1_row6), .row22(video_buffer_1_row22), .row7(video_buffer_1_row7),
    .row23(video_buffer_1_row23), .row8(video_buffer_1_row8), .row24(video_buffer_1_row24),
    .row9(video_buffer_1_row9), .row25(video_buffer_1_row25), .row10(video_buffer_1_row10),
    .row26(video_buffer_1_row26), .row11(video_buffer_1_row11), .row27(video_buffer_1_row27),
    .row12(video_buffer_1_row12), .row28(video_buffer_1_row28), .row13(video_buffer_1_row13),
    .row29(video_buffer_1_row29), .row14(video_buffer_1_row14), .row30(video_buffer_1_row30),
    .row15(video_buffer_1_row15), .row31(video_buffer_1_row31), .data_out(controlled_buffer_1_out));
  // Probe on {adder_1_out[7], vaddr}
  DotMatrix #(.inputtype("row"), .matrixcols(32), .matrixrows(32)) dotmatrix_1 (
    .row0(video_buffer_1_row0), .row1(video_buffer_1_row16), .row2(video_buffer_1_row1),
    .row3(video_buffer_1_row17), .row4(video_buffer_1_row2), .row5(video_buffer_1_row18),
    .row6(video_buffer_1_row3), .row7(video_buffer_1_row19), .row8(video_buffer_1_row4),
    .row9(video_buffer_1_row20), .row10(video_buffer_1_row5), .row11(video_buffer_1_row21),
    .row12(video_buffer_1_row6), .row13(video_buffer_1_row22), .row14(video_buffer_1_row7),
    .row15(video_buffer_1_row23), .row16(video_buffer_1_row8), .row17(video_buffer_1_row24),
    .row18(video_buffer_1_row9), .row19(video_buffer_1_row25), .row20(video_buffer_1_row10),
    .row21(video_buffer_1_row26), .row22(video_buffer_1_row11), .row23(video_buffer_1_row27),
    .row24(video_buffer_1_row12), .row25(video_buffer_1_row28), .row26(video_buffer_1_row13),
    .row27(video_buffer_1_row29), .row28(video_buffer_1_row14), .row29(video_buffer_1_row30),
    .row30(video_buffer_1_row15), .row31(video_buffer_1_row31));
  ROM #(.addrWidth(16)) rom_1 (.addr(cdm_8_mark5_1_p13), .data(controlled_buffer_1_out), .sel(code));
  RAM #(.addrWidth(16)) ram_1 (
    .addr(cdm_8_mark5_1_p13), .data(controlled_buffer_1_out), .sel(data), .clk(clock), .ld(read));  // open: clr
  // Probe on {1'b0, vaddr}
  and and_1 (video, adder_1_out[7], data);

  // Notes on the sheet:
  //   contents of rom_1 (hex, n*v repeats v):
  //   d0 60 d1 ca a1 8c a1 d4
endmodule

module video_buffer (
  input  [7:0] vaddr,
  input  read,
  input  video,
  input  clock,
  input  [7:0] data,
  output [31:0] row0,
  output [31:0] row16,
  output [31:0] row1,
  output [31:0] row17,
  output [7:0] data_out,
  output [31:0] row2,
  output [31:0] row18,
  output [31:0] row3,
  output [31:0] row19,
  output [31:0] row4,
  output [31:0] row20,
  output [31:0] row5,
  output [31:0] row21,
  output [31:0] row6,
  output [31:0] row22,
  output [31:0] row7,
  output [31:0] row23,
  output [31:0] row8,
  output [31:0] row24,
  output [31:0] row9,
  output [31:0] row25,
  output [31:0] row10,
  output [31:0] row26,
  output [31:0] row11,
  output [31:0] row27,
  output [31:0] row12,
  output [31:0] row28,
  output [31:0] row13,
  output [31:0] row29,
  output [31:0] row14,
  output [31:0] row30,
  output [31:0] row15,
  output [31:0] row31
);

  wire and_1_out, and_2_out, decoder_1_out0, decoder_1_out1, decoder_1_out2, decoder_1_out3, decoder_2_out0,
       decoder_2_out1, decoder_2_out2, decoder_2_out3, decoder_2_out4, decoder_2_out5, decoder_2_out6,
       decoder_2_out7, decoder_2_out8, decoder_2_out9, decoder_2_out10, decoder_2_out11, decoder_2_out12,
       decoder_2_out13, decoder_2_out14, decoder_2_out15, decoder_2_out16, decoder_2_out17, decoder_2_out18,
       decoder_2_out19, decoder_2_out20, decoder_2_out21, decoder_2_out22, decoder_2_out23, decoder_2_out24,
       decoder_2_out25, decoder_2_out26, decoder_2_out27, decoder_2_out28, decoder_2_out29, decoder_2_out30,
       decoder_2_out31, not_1_out, not_2_out;
  wire [7:0] multiplexer_1_out, multiplexer_2_out, multiplexer_3_out, multiplexer_4_out, multiplexer_5_out,
       multiplexer_6_out, multiplexer_6_out_2, multiplexer_6_out_3, multiplexer_6_out_4;
  wire [31:0] demultiplexer_1_out0, demultiplexer_1_out1, multiplexer_7_out, multiplexer_8_out, wrow0, wrow1,
       wrow2, wrow3, wrow4, wrow5, wrow6, wrow7, wrow8, wrow9, wrow10, wrow11, wrow12, wrow13, wrow14,
       wrow15, wrow16, wrow17, wrow18, wrow19, wrow20, wrow21, wrow22, wrow23, wrow24, wrow25, wrow26,
       wrow27, wrow28, wrow29, wrow30, wrow31;

  assign data_out = and_1_out ? multiplexer_1_out : 8'bz;  // Controlled_Buffer controlled_buffer_1
  and and_1 (and_1_out, video, read);
  not not_1 (not_1_out, read);
  Multiplexer #(.select(2), .width(8), .enable("false")) multiplexer_1 (
    .in0(multiplexer_6_out_4), .in1(multiplexer_6_out_3), .in2(multiplexer_6_out_2), .in3(multiplexer_6_out),
    .out(multiplexer_1_out), .sel(vaddr[1:0]));
  Decoder #(.select(2), .disabled(0)) decoder_1 (
    .out0(decoder_1_out0), .out1(decoder_1_out1), .out2(decoder_1_out2), .out3(decoder_1_out3),
    .sel(vaddr[1:0]), .en(not_1_out));
  Multiplexer #(.width(8), .enable("false")) multiplexer_2 (
    .in0(multiplexer_6_out_4), .in1(data), .out(multiplexer_2_out), .sel(decoder_1_out0));
  Multiplexer #(.width(8), .enable("false")) multiplexer_3 (
    .in0(multiplexer_6_out_3), .in1(data), .out(multiplexer_3_out), .sel(decoder_1_out1));
  Multiplexer #(.width(8), .enable("false")) multiplexer_4 (
    .in0(multiplexer_6_out_2), .in1(data), .out(multiplexer_4_out), .sel(decoder_1_out2));
  Multiplexer #(.width(8), .enable("false")) multiplexer_5 (
    .in0(multiplexer_6_out), .in1(data), .out(multiplexer_5_out), .sel(decoder_1_out3));
  Demultiplexer #(.width(32)) demultiplexer_1 (
    .out0(demultiplexer_1_out0), .out1(demultiplexer_1_out1),
    .in({multiplexer_2_out, multiplexer_3_out, multiplexer_4_out, multiplexer_5_out}), .sel(vaddr[6]),
    .en(not_1_out));
  Multiplexer #(.width(32), .enable("false")) multiplexer_6 (
    .in0(multiplexer_7_out), .in1(multiplexer_8_out),
    .out({multiplexer_6_out_4, multiplexer_6_out_3, multiplexer_6_out_2, multiplexer_6_out}), .sel(vaddr[6]));
  Multiplexer #(.select(4), .width(32), .enable("false")) multiplexer_7 (
    .in0(row0), .in1(row1), .in2(row2), .in3(row3), .in4(row4), .in5(row5), .in6(row6), .in7(row7),
    .in8(row8), .in9(row9), .in10(row10), .in11(row11), .in12(row12), .in13(row13), .in14(row14),
    .in15(row15), .out(multiplexer_7_out), .sel(vaddr[5:2]));
  Multiplexer #(.select(4), .width(32), .enable("false")) multiplexer_8 (
    .in0(row16), .in1(row17), .in2(row18), .in3(row19), .in4(row20), .in5(row21), .in6(row22), .in7(row23),
    .in8(row24), .in9(row25), .in10(row26), .in11(row27), .in12(row28), .in13(row29), .in14(row30),
    .in15(row31), .out(multiplexer_8_out), .sel(vaddr[5:2]));
  Demultiplexer #(.select(4), .width(32)) demultiplexer_2 (
    .out0(wrow0), .out1(wrow1), .out2(wrow2), .out3(wrow3), .out4(wrow4), .out5(wrow5), .out6(wrow6),
    .out7(wrow7), .out8(wrow8), .out9(wrow9), .out10(wrow10), .out11(wrow11), .out12(wrow12), .out13(wrow13),
    .out14(wrow14), .out15(wrow15), .in(demultiplexer_1_out0), .sel(vaddr[5:2]), .en(not_1_out));
  Demultiplexer #(.select(4), .width(32)) demultiplexer_3 (
    .out0(wrow16), .out1(wrow17), .out2(wrow18), .out3(wrow19), .out4(wrow20), .out5(wrow21), .out6(wrow22),
    .out7(wrow23), .out8(wrow24), .out9(wrow25), .out10(wrow26), .out11(wrow27), .out12(wrow28),
    .out13(wrow29), .out14(wrow30), .out15(wrow31), .in(demultiplexer_1_out1), .sel(vaddr[5:2]),
    .en(not_1_out));
  not not_2 (not_2_out, read);
  and and_2 (and_2_out, video, not_2_out);
  Decoder #(.select(5), .disabled(0)) decoder_2 (
    .out0(decoder_2_out0), .out1(decoder_2_out1), .out2(decoder_2_out2), .out3(decoder_2_out3),
    .out4(decoder_2_out4), .out5(decoder_2_out5), .out6(decoder_2_out6), .out7(decoder_2_out7),
    .out8(decoder_2_out8), .out9(decoder_2_out9), .out10(decoder_2_out10), .out11(decoder_2_out11),
    .out12(decoder_2_out12), .out13(decoder_2_out13), .out14(decoder_2_out14), .out15(decoder_2_out15),
    .out16(decoder_2_out16), .out17(decoder_2_out17), .out18(decoder_2_out18), .out19(decoder_2_out19),
    .out20(decoder_2_out20), .out21(decoder_2_out21), .out22(decoder_2_out22), .out23(decoder_2_out23),
    .out24(decoder_2_out24), .out25(decoder_2_out25), .out26(decoder_2_out26), .out27(decoder_2_out27),
    .out28(decoder_2_out28), .out29(decoder_2_out29), .out30(decoder_2_out30), .out31(decoder_2_out31),
    .sel(vaddr[6:2]), .en(and_2_out));
  Register #(.width(32)) register_1 (.D(wrow0), .en(decoder_2_out0), .Q(row0), .clk(clock));  // open: clr
  Register #(.width(32)) register_2 (.D(wrow1), .en(decoder_2_out1), .Q(row1), .clk(clock));  // open: clr
  Register #(.width(32)) register_3 (.D(wrow2), .en(decoder_2_out2), .Q(row2), .clk(clock));  // open: clr
  Register #(.width(32)) register_4 (.D(wrow3), .en(decoder_2_out3), .Q(row3), .clk(clock));  // open: clr
  Register #(.width(32)) register_5 (.D(wrow4), .en(decoder_2_out4), .Q(row4), .clk(clock));  // open: clr
  Register #(.width(32)) register_6 (.D(wrow5), .en(decoder_2_out5), .Q(row5), .clk(clock));  // open: clr
  Register #(.width(32)) register_7 (.D(wrow6), .en(decoder_2_out6), .Q(row6), .clk(clock));  // open: clr
  Register #(.width(32)) register_8 (.D(wrow7), .en(decoder_2_out7), .Q(row7), .clk(clock));  // open: clr
  Register #(.width(32)) register_9 (.D(wrow8), .en(decoder_2_out8), .Q(row8), .clk(clock));  // open: clr
  Register #(.width(32)) register_10 (.D(wrow9), .en(decoder_2_out9), .Q(row9), .clk(clock));  // open: clr
  Register #(.width(32)) register_11 (.D(wrow10), .en(decoder_2_out10), .Q(row10), .clk(clock));  // open: clr
  Register #(.width(32)) register_12 (.D(wrow11), .en(decoder_2_out11), .Q(row11), .clk(clock));  // open: clr
  Register #(.width(32)) register_13 (.D(wrow12), .en(decoder_2_out12), .Q(row12), .clk(clock));  // open: clr
  Register #(.width(32)) register_14 (.D(wrow13), .en(decoder_2_out13), .Q(row13), .clk(clock));  // open: clr
  Register #(.width(32)) register_15 (.D(wrow14), .en(decoder_2_out14), .Q(row14), .clk(clock));  // open: clr
  Register #(.width(32)) register_16 (.D(wrow15), .en(decoder_2_out15), .Q(row15), .clk(clock));  // open: clr
  Register #(.width(32)) register_17 (.D(wrow16), .en(decoder_2_out16), .Q(row16), .clk(clock));  // open: clr
  Register #(.width(32)) register_18 (.D(wrow17), .en(decoder_2_out17), .Q(row17), .clk(clock));  // open: clr
  Register #(.width(32)) register_19 (.D(wrow18), .en(decoder_2_out18), .Q(row18), .clk(clock));  // open: clr
  Register #(.width(32)) register_20 (.D(wrow19), .en(decoder_2_out19), .Q(row19), .clk(clock));  // open: clr
  Register #(.width(32)) register_21 (.D(wrow20), .en(decoder_2_out20), .Q(row20), .clk(clock));  // open: clr
  Register #(.width(32)) register_22 (.D(wrow21), .en(decoder_2_out21), .Q(row21), .clk(clock));  // open: clr
  Register #(.width(32)) register_23 (.D(wrow22), .en(decoder_2_out22), .Q(row22), .clk(clock));  // open: clr
  Register #(.width(32)) register_24 (.D(wrow23), .en(decoder_2_out23), .Q(row23), .clk(clock));  // open: clr
  Register #(.width(32)) register_25 (.D(wrow24), .en(decoder_2_out24), .Q(row24), .clk(clock));  // open: clr
  Register #(.width(32)) register_26 (.D(wrow25), .en(decoder_2_out25), .Q(row25), .clk(clock));  // open: clr
  Register #(.width(32)) register_27 (.D(wrow26), .en(decoder_2_out26), .Q(row26), .clk(clock));  // open: clr
  Register #(.width(32)) register_28 (.D(wrow27), .en(decoder_2_out27), .Q(row27), .clk(clock));  // open: clr
  Register #(.width(32)) register_29 (.D(wrow28), .en(decoder_2_out28), .Q(row28), .clk(clock));  // open: clr
  Register #(.width(32)) register_30 (.D(wrow29), .en(decoder_2_out29), .Q(row29), .clk(clock));  // open: clr
  Register #(.width(32)) register_31 (.D(wrow30), .en(decoder_2_out30), .Q(row30), .clk(clock));  // open: clr
  Register #(.width(32)) register_32 (.D(wrow31), .en(decoder_2_out31), .Q(row31), .clk(clock));  // open: clr

  // Notes on the sheet:
  //   Data
endmodule
